# Fritzing sketch Thermometr-scheme (saved by Fritzing 0.9.5d)
breadboards: 1

parts:
  Part1 = Arduino Nano (Rev3.0)
  RHT2 = Humidity and Temperature Sensor RHT03
  LCD2 = LCD screen
  LCM1602_IIC1 = LCM1602 IIC [part_number="LCM1602 IIC" chip_label="LCM1602 IIC" package="DIP (Dual Inline) [THT]"]
  R1 = Resistor [tolerance=±5% resistance=220 package=THT]

nets:
  GND: Part1.GND, RHT2.GND_2, LCM1602_IIC1.GND
  N1: Part1.D10, RHT2.Data-signal, R1.Pin_1
  VCC: Part1.5V, RHT2.Vcc, LCM1602_IIC1.VCC, R1.Pin_0
  N2: Part1.A5, LCM1602_IIC1.SCL
  N3: Part1.A4, LCM1602_IIC1.SDA
  N4: LCD2.VSS, LCM1602_IIC1.K
  N5: LCM1602_IIC1.LED_A, LCM1602_IIC1.LED_B

notes:
  I2C shield
  analog
  ground
  resistor
  data from DHT22
  DHT22
  LCD-1602

custom parts:
  LCM1602 IIC: I2C-Module to use a 1602 or 2004 LCD on with the wire.h libory Serial LCD Modul
